// Logisim project 224 project.circ as structural Verilog: 1 circuit, main circuit main
module main (
);

  wire undriven_3;
  wire [2:0] undriven_2, undriven_4, undriven_5;
  wire [15:0] demultiplexer_1_out0, demultiplexer_1_out1, demultiplexer_1_out2, demultiplexer_1_out3,
       demultiplexer_1_out4, demultiplexer_1_out5, demultiplexer_1_out6, demultiplexer_1_out7,
       multiplexer_1_out, multiplexer_2_out, register_1_q, register_2_q, register_3_q, register_6_q,
       register_7_q, register_8_q, undriven;

  Demultiplexer #(.select(3), .width(16), .enable("false")) demultiplexer_1 (
    .out0(demultiplexer_1_out0), .out1(demultiplexer_1_out1), .out2(demultiplexer_1_out2),
    .out3(demultiplexer_1_out3), .out4(demultiplexer_1_out4), .out5(demultiplexer_1_out5),
    .out6(demultiplexer_1_out6), .out7(demultiplexer_1_out7), .in(undriven), .sel(undriven_2));
  Adder #(.width(16)) adder_1 ();  // open: a, b, out, cin, cout
  Register #(.width(16), .trigger("high")) register_1 (
    .D(demultiplexer_1_out0), .Q(register_1_q), .clk(undriven_3));  // open: en, clr
  Register #(.width(16), .trigger("high")) register_2 (
    .D(demultiplexer_1_out1), .Q(register_2_q), .clk(undriven_3));  // open: en, clr
  Register #(.width(16), .trigger("high")) register_3 (
    .D(demultiplexer_1_out2), .Q(register_3_q), .clk(undriven_3));  // open: en, clr
  Register #(.width(16), .trigger("high")) register_4 (
    .D(demultiplexer_1_out3), .Q(register_3_q), .clk(undriven_3));  // open: en, clr
  Register #(.width(16), .trigger("high")) register_5 (
    .D(demultiplexer_1_out4), .Q(register_3_q), .clk(undriven_3));  // open: en, clr
  Register #(.width(16), .trigger("high")) register_6 (
    .D(demultiplexer_1_out5), .Q(register_6_q), .clk(undriven_3));  // open: en, clr
  Register #(.width(16), .trigger("high")) register_7 (
    .D(demultiplexer_1_out6), .Q(register_7_q), .clk(undriven_3));  // open: en, clr
  Register #(.width(16), .trigger("high")) register_8 (
    .D(demultiplexer_1_out7), .Q(register_8_q), .clk(undriven_3));  // open: en, clr
  Subtractor subtractor_1 ();  // open: a, b, out, bin, bout
  Multiplexer #(.select(3), .width(16), .enable("false")) multiplexer_1 (
    .in0(register_1_q), .in1(register_2_q), .in2(register_3_q), .in3(register_3_q), .in4(register_3_q),
    .in5(register_6_q), .in6(register_7_q), .in7(register_8_q), .out(multiplexer_1_out), .sel(undriven_4));
  Multiplexer #(.select(3), .width(16), .enable("false")) multiplexer_2 (
    .in0(register_1_q), .in1(register_2_q), .in2(register_3_q), .in3(register_3_q), .in4(register_3_q),
    .in5(register_6_q), .in6(register_7_q), .in7(register_8_q), .out(multiplexer_2_out), .sel(undriven_5));

  // Notes on the sheet:
  //   RF_DATA_IN
  //   RF_AD_IN
  //   RF_WR
  //   RF_AD_OUT2
  //   RF_AD_OUT1
  //   RF_DATA_OUT2
  //   RF_DATA_OUT1
endmodule
